// Logisim project decoding_logic.circ as structural Verilog: 2 circuits, main circuit main
module main (
  input  A5,
  input  A6,
  input  A7,
  input  A15,
  input  IORQ,
  output I_O_Port_0,
  output I_O_Port_1,
  output I_O_Port_2,
  output I_O_Port_3,
  output I_O_Port_4,
  output I_O_Port_5,
  output I_O_Port_6,
  output I_O_Port_7,
  output RAM_EN,
  output ROM_EN
);

  wire not_1_out, not_2_out;

  not not_1 (not_1_out, A15);
  not not_2 (not_2_out, IORQ);
  or or_1 (RAM_EN, not_1_out, not_2_out);
  or or_2 (ROM_EN, not_2_out, A15);
  SN74HC138N_Active_low_3_8_decoder sn74hc138n_active_low_3_8_decoder_1 (
    .Enable(IORQ), .Input({A7, A6, A5}),
    .out_3({I_O_Port_7, I_O_Port_6, I_O_Port_5, I_O_Port_4, I_O_Port_3, I_O_Port_2, I_O_Port_1, I_O_Port_0}));
endmodule

module SN74HC138N_Active_low_3_8_decoder (
  input  Enable,
  input  [2:0] Input,
  output [7:0] out_3
);

  wire decoder_1_out0, decoder_1_out1, decoder_1_out2, decoder_1_out3, decoder_1_out4, decoder_1_out5,
       decoder_1_out6, decoder_1_out7, not_1_out;

  not not_1 (not_1_out, Enable);
  Decoder #(.select(3), .disabled(0)) decoder_1 (
    .out0(decoder_1_out0), .out1(decoder_1_out1), .out2(decoder_1_out2), .out3(decoder_1_out3),
    .out4(decoder_1_out4), .out5(decoder_1_out5), .out6(decoder_1_out6), .out7(decoder_1_out7), .sel(Input),
    .en(not_1_out));
  not not_2 (out_3[0], decoder_1_out0);
  not not_3 (out_3[1], decoder_1_out1);
  not not_4 (out_3[2], decoder_1_out2);
  not not_5 (out_3[3], decoder_1_out3);
  not not_6 (out_3[4], decoder_1_out4);
  not not_7 (out_3[5], decoder_1_out5);
  not not_8 (out_3[6], decoder_1_out6);
  not not_9 (out_3[7], decoder_1_out7);

  // Notes on the sheet:
  //   Enable is active-low
endmodule
