# Fritzing sketch pato (saved by Fritzing 0.9.3b)
perfboards: 1

parts:
  Zilog_Z80 = Z80 A [package="DIP (Dual Inline) [THT]"]
  ALLIANCE_AS6C62256 = IC, DIP package, 28 pins [chip_label=IC]
  J1 = male pin header, 24 pins [form="♂ (male)"]  # not connected
  Atmel_AT28C64B = IC, DIP package, 28 pins [chip_label=IC]
  C1 = Ceramic Capacitor [capacitance=100nF package="100 mil [THT, multilayer]"]
  C2 = Ceramic Capacitor [capacitance=100nF package="100 mil [THT, multilayer]"]  # not connected

nets:
  N1: Zilog_Z80.+5V, C1.1
  N2: Zilog_Z80.GND, ALLIANCE_AS6C62256.pin14, Atmel_AT28C64B.pin14, C1.0

custom parts:
  Z80 A: Zilog Z80 A CPU
