// Logisim project uart-decoding-logic.circ as structural Verilog: 1 circuit, main circuit main
module main (
  input  Rx,
  input  Clear,
  input  Wr,
  input  in_4,
  input  in_5,
  input  in_6,
  input  in_7,
  input  in_8,
  input  in_9,
  input  in_10,
  input  in_11,
  output out_12,
  output out_13,
  output out_14,
  output out_15,
  output out_16,
  output out_17,
  output out_18,
  output out_19,
  output Tx
);

  wire and_1_out, and_2_out, and_3_out, clock_1_out, not_1_out, not_2_out, not_3_out, shift_register_1_out,
       shift_register_4_q0, shift_register_4_q1, undriven;
  wire [3:0] Clock_demultiplier_q;

  Shift_Register shift_register_1 (
    .in(1'b1), .clk(undriven), .out(shift_register_1_out), .load(Wr), .d0(1'b1), .d1(1'b1), .d2(1'b1),
    .d3(1'b1), .d4(1'b1), .d5(1'b1), .d6(in_4), .d7(in_5));  // open: shift, clr, q0, q1, q2, q3, q4, q5, q6, q7
  Shift_Register shift_register_2 (
    .in(Rx), .clk(and_1_out), .clr(Clear), .q0(out_12), .q1(out_13), .q2(out_14), .q3(out_15), .q4(out_16),
    .q5(out_17), .q6(out_18), .q7(out_19));  // open: shift, out, load, d0, d1, d2, d3, d4, d5, d6, d7
  Shift_Register shift_register_3 (
    .in(shift_register_1_out), .clk(undriven), .out(Tx), .load(Wr), .d0(in_6), .d1(in_7), .d2(in_8),
    .d3(in_9), .d4(in_10), .d5(in_11), .d6(1'b0), .d7(1'b1));  // open: shift, clr, q0, q1, q2, q3, q4, q5, q6, q7
  Shift_Register shift_register_4 (
    .in(out_19), .clk(and_1_out), .clr(Clear), .q0(shift_register_4_q0), .q1(shift_register_4_q1));  // open: shift, out, load, d0, d1, d2, q2, d3, q3, d4, q4, d5, q5, d6, q6, d7, q7
  not not_1 (not_1_out, shift_register_4_q0);
  and and_1 (and_1_out, not_2_out, Clock_demultiplier_q[2]);
  and and_2 (and_2_out, shift_register_4_q1, not_1_out);
  not not_2 (not_2_out, and_2_out);
  Counter #(.width(4), .max('hf), .trigger("falling")) Clock_demultiplier (
    .Q(Clock_demultiplier_q), .clk(clock_1_out), .clr(and_3_out));  // open: load, D, count, carry
  and and_3 (and_3_out, not_3_out, clock_1_out);
  not not_3 (not_3_out, Rx);
  Clock clock_1 (.out(clock_1_out));
endmodule
