// Logisim project wip_delay.circ as structural Verilog: 1 circuit, main circuit main
module main (
  input  Rx
);

  wire clock_1_out, nand_1_out;
  wire [7:0] counter_1_q;

  Counter counter_1 (.Q(counter_1_q), .clk(clock_1_out), .clr(nand_1_out));  // open: load, D, count, carry
  Clock clock_1 (.out(clock_1_out));
  nand nand_1 (nand_1_out, counter_1_q[7], Rx);
endmodule
